// Logisim project ProcessorCoreDesign.circ as structural Verilog: 12 circuits, main circuit main
module main (
  input  reset
);

  wire ALUinB, and_1_out, and_2_out, BRE, BRG, clk, DMwe, greater, \input , J, JAL, JP, keyboard_1_avail,
       memory_latch_1_oe_latched, memory_latch_1_we_latched, notclk, or_1_out, \output , Rwd, Rwe, zero;
  wire [1:0] Rdst;
  wire [2:0] ALUop, multiplexer_10_out, Rd, Rs, Rt, shamt;
  wire [3:0] Opcode;
  wire [5:0] Immed;
  wire [6:0] keyboard_1_data;
  wire [7:0] rdout;
  wire [11:0] Address;
  wire [15:0] alu_1_out16, ALUout, bit_extender_1_out, bit_extender_2_out, memory_latch_1_address_latched,
       memory_latch_1_data_in_latched, multiplexer_1_out, multiplexer_2_out, multiplexer_11_out,
       multiplexer_12_out, multiplexer_13_out, multiplexer_15_out, out, PC1, programcounter_1_output,
       ram_1_dout, rom_1_data, Rsout, tunRt;

  ProgramCounter programcounter_1 (
    .clk(clk), .reset(reset), .\output (programcounter_1_output), .\input (multiplexer_15_out));
  ROM #(.addrWidth(16), .dataWidth(16)) rom_1 (.addr(programcounter_1_output), .data(rom_1_data));
  Clock u_clk (.out(clk));
  multiadder multiadder_1 (.result(PC1), .in1(programcounter_1_output), .in2(16'h1));  // open: ovf, sub
  TTY #(.rows(13), .cols(80), .trigger("falling")) tty_1 (.data(Rsout[6:0]), .clk(clk), .we(\output ), .clr(reset));
  Keyboard keyboard_1 (.clk(clk), .re(\input ), .clr(reset), .avail(keyboard_1_avail), .data(keyboard_1_data));
  not not_1 (notclk, clk);
  InstrDecode instrdecode_1 (
    .in1(rom_1_data), .Rd(Rd), .Rs(Rs), .Rt(Rt), .shamt(shamt), .Immed(Immed), .Address(Address),
    .opcode(Opcode));
  Multiplexer #(.width(16), .enable("false")) multiplexer_1 (
    .in0(out), .in1({{8{1'b0}}, rdout}), .out(multiplexer_1_out), .sel(\input ));
  control control_1 (
    .Rdst(Rdst), .ALUop(ALUop), .Rwe(Rwe), .opcode(Opcode), .BRE(BRE), .JP(JP), .DMwe(DMwe), .Rwd(Rwd),
    .ALUinB(ALUinB), .Jal(JAL), .Jr(J), .\output (\output ), .\input (\input ), .BRG(BRG));
  Multiplexer #(.width(16), .enable("false")) multiplexer_2 (
    .in0(multiplexer_1_out), .in1(PC1), .out(multiplexer_2_out), .sel(JAL));
  Multiplexer #(.enable("false")) multiplexer_3 (
    .in0(1'b0), .in1(keyboard_1_data[0]), .out(rdout[0]), .sel(keyboard_1_avail));
  Multiplexer #(.enable("false")) multiplexer_4 (
    .in0(1'b0), .in1(keyboard_1_data[1]), .out(rdout[1]), .sel(keyboard_1_avail));
  Multiplexer #(.enable("false")) multiplexer_5 (
    .in0(1'b0), .in1(keyboard_1_data[2]), .out(rdout[2]), .sel(keyboard_1_avail));
  Multiplexer #(.enable("false")) multiplexer_6 (
    .in0(1'b0), .in1(keyboard_1_data[3]), .out(rdout[3]), .sel(keyboard_1_avail));
  Multiplexer #(.enable("false")) multiplexer_7 (
    .in0(1'b0), .in1(keyboard_1_data[4]), .out(rdout[4]), .sel(keyboard_1_avail));
  Multiplexer #(.enable("false")) multiplexer_8 (
    .in0(1'b0), .in1(keyboard_1_data[5]), .out(rdout[5]), .sel(keyboard_1_avail));
  Multiplexer #(.enable("false")) multiplexer_9 (
    .in0(1'b0), .in1(keyboard_1_data[6]), .out(rdout[6]), .sel(keyboard_1_avail));
  assign bit_extender_1_out = {{4{Address[11]}}, Address};  // Bit_Extender bit_extender_1
  memory_latch memory_latch_1 (
    .address(ALUout), .WE(DMwe), .clk(clk), .data_in(tunRt),
    .address_latched(memory_latch_1_address_latched), .WE_latched(memory_latch_1_we_latched),
    .OE_latched(memory_latch_1_oe_latched), .data_in_latched(memory_latch_1_data_in_latched));
  RegisterFile registerfile_1 (
    .rd(multiplexer_10_out), .clk(notclk), .reset(reset), .rs1(Rs), .data_in(multiplexer_2_out), .rs2(Rt),
    .rs1_content(Rsout), .rs2_content(tunRt), .write_enable(Rwe));
  Multiplexer #(.select(2), .width(3), .enable("false")) multiplexer_10 (
    .in0(Rt), .in1(Rd), .in2(3'b111), .out(multiplexer_10_out), .sel(Rdst));  // open: in3
  RAM #(.addrWidth(16), .dataWidth(16), .trigger("high"), .databus("bibus")) ram_1 (
    .addr(memory_latch_1_address_latched), .we(memory_latch_1_we_latched), .oe(memory_latch_1_oe_latched),
    .din(memory_latch_1_data_in_latched), .dout(ram_1_dout));
  alu alu_1 (.a(PC1), .b(bit_extender_2_out), .out16(alu_1_out16), .optype(3'b000));  // open: outbeq, shamt, outbgt
  assign bit_extender_2_out = {{10{Immed[5]}}, Immed};  // Bit_Extender bit_extender_2
  not not_2 (rdout[7], keyboard_1_avail);
  and and_1 (and_1_out, BRE, zero);
  or or_1 (or_1_out, and_1_out, and_2_out);
  Multiplexer #(.width(16), .enable("false")) multiplexer_11 (
    .in0(tunRt), .in1(bit_extender_2_out), .out(multiplexer_11_out), .sel(ALUinB));
  and and_2 (and_2_out, BRG, greater);
  Multiplexer #(.width(16), .enable("false")) multiplexer_12 (
    .in0(PC1), .in1(alu_1_out16), .out(multiplexer_12_out), .sel(or_1_out));
  Multiplexer #(.width(16), .enable("false")) multiplexer_13 (
    .in0(multiplexer_12_out), .in1(bit_extender_1_out), .out(multiplexer_13_out), .sel(JP));
  alu alu_2 (
    .a(Rsout), .b(multiplexer_11_out), .outbeq(zero), .out16(ALUout), .shamt(shamt), .optype(ALUop),
    .outbgt(greater));
  Multiplexer #(.width(16), .enable("false")) multiplexer_14 (.in0(ALUout), .in1(ram_1_dout), .out(out), .sel(Rwd));
  Multiplexer #(.width(16), .enable("false")) multiplexer_15 (
    .in0(multiplexer_13_out), .in1(Rsout), .out(multiplexer_15_out), .sel(J));

  // Other names for the same wires on the sheet: TTYin[6:0] = Rsout[6:0]
endmodule

module register (
  input  [15:0] info_in,
  input  clock,
  input  write_enable,
  input  reset,
  output [15:0] info_out
);

  wire and_1_out;

  and and_1 (and_1_out, clock, write_enable);
  D_Flip_Flop d_ff_1 (.D(info_in[0]), .clk(and_1_out), .Q(info_out[0]), .reset(reset));  // open: Qn, preset
  D_Flip_Flop d_ff_2 (.D(info_in[1]), .clk(and_1_out), .Q(info_out[1]), .reset(reset));  // open: Qn, preset
  D_Flip_Flop d_ff_3 (.D(info_in[2]), .clk(and_1_out), .Q(info_out[2]), .reset(reset));  // open: Qn, preset
  D_Flip_Flop d_ff_4 (.D(info_in[3]), .clk(and_1_out), .Q(info_out[3]), .reset(reset));  // open: Qn, preset
  D_Flip_Flop d_ff_5 (.D(info_in[4]), .clk(and_1_out), .Q(info_out[4]), .reset(reset));  // open: Qn, preset
  D_Flip_Flop d_ff_6 (.D(info_in[5]), .clk(and_1_out), .Q(info_out[5]), .reset(reset));  // open: Qn, preset
  D_Flip_Flop d_ff_7 (.D(info_in[6]), .clk(and_1_out), .Q(info_out[6]), .reset(reset));  // open: Qn, preset
  D_Flip_Flop d_ff_8 (.D(info_in[7]), .clk(and_1_out), .Q(info_out[7]), .reset(reset));  // open: Qn, preset
  D_Flip_Flop d_ff_9 (.D(info_in[8]), .clk(and_1_out), .Q(info_out[8]), .reset(reset));  // open: Qn, preset
  D_Flip_Flop d_ff_10 (.D(info_in[9]), .clk(and_1_out), .Q(info_out[9]), .reset(reset));  // open: Qn, preset
  D_Flip_Flop d_ff_11 (.D(info_in[10]), .clk(and_1_out), .Q(info_out[10]), .reset(reset));  // open: Qn, preset
  D_Flip_Flop d_ff_12 (.D(info_in[11]), .clk(and_1_out), .Q(info_out[11]), .reset(reset));  // open: Qn, preset
  D_Flip_Flop d_ff_13 (.D(info_in[12]), .clk(and_1_out), .Q(info_out[12]), .reset(reset));  // open: Qn, preset
  D_Flip_Flop d_ff_14 (.D(info_in[13]), .clk(and_1_out), .Q(info_out[13]), .reset(reset));  // open: Qn, preset
  D_Flip_Flop d_ff_15 (.D(info_in[14]), .clk(and_1_out), .Q(info_out[14]), .reset(reset));  // open: Qn, preset
  D_Flip_Flop d_ff_16 (.D(info_in[15]), .clk(and_1_out), .Q(info_out[15]), .reset(reset));  // open: Qn, preset

  // Other names for the same wires on the sheet: in0 = info_in[0]; in1 = info_in[1]; in2 = info_in[2];
  //   in3 = info_in[3]; in4 = info_in[4]; in5 = info_in[5]; in6 = info_in[6]; in7 = info_in[7]; in8 = info_in[8];
  //   in9 = info_in[9]; in10 = info_in[10]; in11 = info_in[11]; in12 = info_in[12]; in13 = info_in[13];
  //   in14 = info_in[14]; in15 = info_in[15]
endmodule

module RegisterFile (
  input  write_enable,
  input  [2:0] rd,
  input  clk,
  input  reset,
  input  [2:0] rs1,
  input  [15:0] data_in,
  input  [2:0] rs2,
  output [15:0] rs1_content,
  output [15:0] rs2_content
);

  wire decoder_1_out1, decoder_1_out2, decoder_1_out3, decoder_1_out4, decoder_1_out5, decoder_1_out6,
       decoder_1_out7;
  wire [15:0] r1tun, r2tun, r3tun, r4tun, r5tun, r6tun, r7tun;

  Decoder #(.select(3)) decoder_1 (
    .out1(decoder_1_out1), .out2(decoder_1_out2), .out3(decoder_1_out3), .out4(decoder_1_out4),
    .out5(decoder_1_out5), .out6(decoder_1_out6), .out7(decoder_1_out7), .sel(rd), .en(write_enable));  // open: out0
  register register_1 (.info_in(data_in), .clock(clk), .write_enable(decoder_1_out1), .reset(reset), .info_out(r1tun));
  register register_2 (.info_in(data_in), .clock(clk), .write_enable(decoder_1_out2), .reset(reset), .info_out(r2tun));
  register register_3 (.info_in(data_in), .clock(clk), .write_enable(decoder_1_out3), .reset(reset), .info_out(r3tun));
  register register_4 (.info_in(data_in), .clock(clk), .write_enable(decoder_1_out4), .reset(reset), .info_out(r4tun));
  register register_5 (.info_in(data_in), .clock(clk), .write_enable(decoder_1_out5), .reset(reset), .info_out(r5tun));
  register register_6 (.info_in(data_in), .clock(clk), .write_enable(decoder_1_out6), .reset(reset), .info_out(r6tun));
  register register_7 (.info_in(data_in), .clock(clk), .write_enable(decoder_1_out7), .reset(reset), .info_out(r7tun));
  // Probe on {16{1'b0}}
  // Probe on r1tun
  // Probe on r2tun
  // Probe on r3tun
  // Probe on r4tun
  // Probe on r5tun
  // Probe on r6tun
  // Probe on r7tun
  Multiplexer #(.select(3), .width(16), .enable("false")) multiplexer_1 (
    .in0({16{1'b0}}), .in1(r1tun), .in2(r2tun), .in3(r3tun), .in4(r4tun), .in5(r5tun), .in6(r6tun),
    .in7(r7tun), .out(rs1_content), .sel(rs1));
  Multiplexer #(.select(3), .width(16), .enable("false")) multiplexer_2 (
    .in0({16{1'b0}}), .in1(r1tun), .in2(r2tun), .in3(r3tun), .in4(r4tun), .in5(r5tun), .in6(r6tun),
    .in7(r7tun), .out(rs2_content), .sel(rs2));

  // Other names for the same wires on the sheet: datatun[15:0] = data_in; resettun = reset
endmodule

module alu (
  input  [15:0] a,
  input  [15:0] b,
  input  [2:0] shamt,
  input  [2:0] optype,
  output outbeq,
  output outbgt,
  output [15:0] out16
);

  wire multiadder_1_p3, not_1_out, not_2_out;
  wire [15:0] and_1_out, leftshift_1_result, multiadder_1_p5, multiadder_2_result, or_1_out,
       rightshift_1_result;

  // multiadder multiadder_1: pin names not known; wires that end beside it: a, b, multiadder_1_p3, multiadder_1_p3, multiadder_1_p5
  multiadder multiadder_2 (.result(multiadder_2_result), .in1(a), .in2(b), .sub(1'b1));  // open: ovf
  assign or_1_out = a | b;  // OR_Gate or_1, 16 bits wide
  assign and_1_out = a & b;  // AND_Gate and_1, 16 bits wide
  leftshift leftshift_1 (.\input (a), .result(leftshift_1_result), .shiftcount(shamt));
  rightshift rightshift_1 (.\input (a), .result(rightshift_1_result), .shiftcount(shamt));
  not not_1 (not_1_out, out16[15]);
  nor nor_1 (outbeq, out16[0], out16[1], out16[2], out16[3], out16[4], out16[5], out16[6], out16[7], out16[8], out16[9], out16[10], out16[11], out16[12], out16[13], out16[14], out16[15]);
  Multiplexer #(.select(3), .width(16), .enable("false")) multiplexer_1 (
    .in0(multiadder_1_p5), .in1(multiadder_2_result), .in2(or_1_out), .in3(and_1_out),
    .in4(leftshift_1_result), .in5(rightshift_1_result), .out(out16), .sel(optype));  // open: in6, in7
  not not_2 (not_2_out, outbeq);
  and and_2 (outbgt, not_2_out, not_1_out);

  // Other names for the same wires on the sheet: atun[15:0] = a; btun[15:0] = b; shift[2:0] = shamt
endmodule

module adder (
  input  in,
  input  A,
  input  B,
  output Sum,
  output out
);

  wire and_1_out, and_2_out, xor_1_out;

  and and_1 (and_1_out, B, A);
  xor xor_1 (xor_1_out, A, B);
  or or_1 (out, and_1_out, and_2_out);
  and and_2 (and_2_out, xor_1_out, in);
  xor xor_2 (Sum, in, xor_1_out);
endmodule

module multiadder (
  input  [15:0] in1,
  input  [15:0] in2,
  input  sub,
  output [15:0] result,
  output ovf
);

  wire adder_1_out, adder_2_out, adder_3_out, adder_4_out, adder_5_out, adder_6_out, adder_7_out,
       adder_8_out, adder_9_out, adder_10_out, adder_11_out, adder_12_out, adder_13_out, adder_14_out,
       adder_15_out, adder_16_out, xor_1_out, xor_2_out, xor_3_out, xor_4_out, xor_5_out, xor_6_out,
       xor_7_out, xor_8_out, xor_9_out, xor_10_out, xor_11_out, xor_12_out, xor_13_out, xor_14_out,
       xor_15_out, xor_16_out;

  xor xor_1 (xor_1_out, in2[0], sub);
  xor xor_2 (xor_2_out, in2[1], sub);
  xor xor_3 (xor_3_out, in2[2], sub);
  xor xor_4 (xor_4_out, in2[3], sub);
  xor xor_5 (xor_5_out, in2[4], sub);
  xor xor_6 (xor_6_out, in2[5], sub);
  xor xor_7 (xor_7_out, in2[6], sub);
  xor xor_8 (xor_8_out, in2[7], sub);
  xor xor_9 (xor_9_out, in2[8], sub);
  xor xor_10 (xor_10_out, in2[9], sub);
  xor xor_11 (xor_11_out, in2[10], sub);
  xor xor_12 (xor_12_out, in2[11], sub);
  xor xor_13 (xor_13_out, in2[12], sub);
  xor xor_14 (xor_14_out, in2[13], sub);
  xor xor_15 (xor_15_out, in2[14], sub);
  xor xor_16 (xor_16_out, in2[15], sub);
  adder adder_1 (.A(xor_1_out), .B(in1[0]), .Sum(result[0]), .in(sub), .out(adder_1_out));
  adder adder_2 (.A(xor_2_out), .B(in1[1]), .Sum(result[1]), .in(adder_1_out), .out(adder_2_out));
  adder adder_3 (.A(xor_3_out), .B(in1[2]), .Sum(result[2]), .in(adder_2_out), .out(adder_3_out));
  adder adder_4 (.A(xor_4_out), .B(in1[3]), .Sum(result[3]), .in(adder_3_out), .out(adder_4_out));
  adder adder_5 (.A(xor_5_out), .B(in1[4]), .Sum(result[4]), .in(adder_4_out), .out(adder_5_out));
  adder adder_6 (.A(xor_6_out), .B(in1[5]), .Sum(result[5]), .in(adder_5_out), .out(adder_6_out));
  adder adder_7 (.A(xor_7_out), .B(in1[6]), .Sum(result[6]), .in(adder_6_out), .out(adder_7_out));
  adder adder_8 (.A(xor_8_out), .B(in1[7]), .Sum(result[7]), .in(adder_7_out), .out(adder_8_out));
  adder adder_9 (.A(xor_9_out), .B(in1[8]), .Sum(result[8]), .in(adder_8_out), .out(adder_9_out));
  adder adder_10 (.A(xor_10_out), .B(in1[9]), .Sum(result[9]), .in(adder_9_out), .out(adder_10_out));
  adder adder_11 (.A(xor_11_out), .B(in1[10]), .Sum(result[10]), .in(adder_10_out), .out(adder_11_out));
  adder adder_12 (.A(xor_12_out), .B(in1[11]), .Sum(result[11]), .in(adder_11_out), .out(adder_12_out));
  adder adder_13 (.A(xor_13_out), .B(in1[12]), .Sum(result[12]), .in(adder_12_out), .out(adder_13_out));
  adder adder_14 (.A(xor_14_out), .B(in1[13]), .Sum(result[13]), .in(adder_13_out), .out(adder_14_out));
  adder adder_15 (.A(xor_15_out), .B(in1[14]), .Sum(result[14]), .in(adder_14_out), .out(adder_15_out));
  adder adder_16 (.A(xor_16_out), .B(in1[15]), .Sum(result[15]), .in(adder_15_out), .out(adder_16_out));
  xor xor_17 (ovf, adder_15_out, adder_16_out);

  // Other names for the same wires on the sheet: A0 = in1[0]; A1 = in1[1]; A2 = in1[2]; A3 = in1[3]; A4 = in1[4];
  //   A5 = in1[5]; A6 = in1[6]; A7 = in1[7]; A8 = in1[8]; A9 = in1[9]; A10 = in1[10]; A11 = in1[11]; A12 = in1[12];
  //   A13 = in1[13]; A14 = in1[14]; A15 = in1[15]; B0 = in2[0]; B1 = in2[1]; B2 = in2[2]; B3 = in2[3]; B4 = in2[4];
  //   B5 = in2[5]; B6 = in2[6]; B7 = in2[7]; B8 = in2[8]; B9 = in2[9]; B10 = in2[10]; B11 = in2[11]; B12 = in2[12];
  //   B13 = in2[13]; B14 = in2[14]; B15 = in2[15]; S0 = result[0]; S1 = result[1]; S2 = result[2]; S3 = result[3];
  //   S4 = result[4]; S5 = result[5]; S6 = result[6]; S7 = result[7]; S8 = result[8]; S9 = result[9];
  //   S10 = result[10]; S11 = result[11]; S12 = result[12]; S13 = result[13]; S14 = result[14]; S15 = result[15]
endmodule

module leftshift (
  input  [2:0] shiftcount,
  input  [15:0] \input ,
  output [15:0] result
);

  wire multiplexer_1_out, multiplexer_2_out, multiplexer_3_out, multiplexer_4_out, multiplexer_5_out,
       multiplexer_6_out, multiplexer_7_out, multiplexer_8_out, multiplexer_9_out, multiplexer_10_out,
       multiplexer_11_out, multiplexer_12_out, multiplexer_13_out, multiplexer_14_out, multiplexer_15_out,
       multiplexer_16_out, multiplexer_17_out, multiplexer_18_out, multiplexer_19_out, multiplexer_20_out,
       multiplexer_21_out, multiplexer_22_out, multiplexer_23_out, multiplexer_24_out, multiplexer_25_out,
       multiplexer_26_out, multiplexer_27_out, multiplexer_28_out, multiplexer_29_out, multiplexer_30_out,
       multiplexer_31_out, multiplexer_32_out;

  Multiplexer #(.enable("false")) multiplexer_1 (
    .in0(\input [15]), .in1(\input [14]), .out(multiplexer_1_out), .sel(shiftcount[0]));
  Multiplexer #(.enable("false")) multiplexer_2 (
    .in0(\input [14]), .in1(\input [13]), .out(multiplexer_2_out), .sel(shiftcount[0]));
  Multiplexer #(.enable("false")) multiplexer_3 (
    .in0(\input [13]), .in1(\input [12]), .out(multiplexer_3_out), .sel(shiftcount[0]));
  Multiplexer #(.enable("false")) multiplexer_4 (
    .in0(\input [12]), .in1(\input [11]), .out(multiplexer_4_out), .sel(shiftcount[0]));
  Multiplexer #(.enable("false")) multiplexer_5 (
    .in0(\input [11]), .in1(\input [10]), .out(multiplexer_5_out), .sel(shiftcount[0]));
  Multiplexer #(.enable("false")) multiplexer_6 (
    .in0(\input [10]), .in1(\input [9]), .out(multiplexer_6_out), .sel(shiftcount[0]));
  Multiplexer #(.enable("false")) multiplexer_7 (
    .in0(\input [9]), .in1(\input [8]), .out(multiplexer_7_out), .sel(shiftcount[0]));
  Multiplexer #(.enable("false")) multiplexer_8 (
    .in0(\input [8]), .in1(\input [7]), .out(multiplexer_8_out), .sel(shiftcount[0]));
  Multiplexer #(.enable("false")) multiplexer_9 (
    .in0(\input [7]), .in1(\input [6]), .out(multiplexer_9_out), .sel(shiftcount[0]));
  Multiplexer #(.enable("false")) multiplexer_10 (
    .in0(\input [6]), .in1(\input [5]), .out(multiplexer_10_out), .sel(shiftcount[0]));
  Multiplexer #(.enable("false")) multiplexer_11 (
    .in0(\input [5]), .in1(\input [4]), .out(multiplexer_11_out), .sel(shiftcount[0]));
  Multiplexer #(.enable("false")) multiplexer_12 (
    .in0(\input [4]), .in1(\input [3]), .out(multiplexer_12_out), .sel(shiftcount[0]));
  Multiplexer #(.enable("false")) multiplexer_13 (
    .in0(\input [3]), .in1(\input [2]), .out(multiplexer_13_out), .sel(shiftcount[0]));
  Multiplexer #(.enable("false")) multiplexer_14 (
    .in0(\input [2]), .in1(\input [1]), .out(multiplexer_14_out), .sel(shiftcount[0]));
  Multiplexer #(.enable("false")) multiplexer_15 (
    .in0(\input [1]), .in1(\input [0]), .out(multiplexer_15_out), .sel(shiftcount[0]));
  Multiplexer #(.enable("false")) multiplexer_16 (
    .in0(\input [0]), .in1(1'b0), .out(multiplexer_16_out), .sel(shiftcount[0]));
  Multiplexer #(.enable("false")) multiplexer_17 (
    .in0(multiplexer_1_out), .in1(multiplexer_3_out), .out(multiplexer_17_out), .sel(shiftcount[1]));
  Multiplexer #(.enable("false")) multiplexer_18 (
    .in0(multiplexer_2_out), .in1(multiplexer_4_out), .out(multiplexer_18_out), .sel(shiftcount[1]));
  Multiplexer #(.enable("false")) multiplexer_19 (
    .in0(multiplexer_3_out), .in1(multiplexer_5_out), .out(multiplexer_19_out), .sel(shiftcount[1]));
  Multiplexer #(.enable("false")) multiplexer_20 (
    .in0(multiplexer_4_out), .in1(multiplexer_6_out), .out(multiplexer_20_out), .sel(shiftcount[1]));
  Multiplexer #(.enable("false")) multiplexer_21 (
    .in0(multiplexer_5_out), .in1(multiplexer_7_out), .out(multiplexer_21_out), .sel(shiftcount[1]));
  Multiplexer #(.enable("false")) multiplexer_22 (
    .in0(multiplexer_6_out), .in1(multiplexer_8_out), .out(multiplexer_22_out), .sel(shiftcount[1]));
  Multiplexer #(.enable("false")) multiplexer_23 (
    .in0(multiplexer_7_out), .in1(multiplexer_9_out), .out(multiplexer_23_out), .sel(shiftcount[1]));
  Multiplexer #(.enable("false")) multiplexer_24 (
    .in0(multiplexer_8_out), .in1(multiplexer_10_out), .out(multiplexer_24_out), .sel(shiftcount[1]));
  Multiplexer #(.enable("false")) multiplexer_25 (
    .in0(multiplexer_9_out), .in1(multiplexer_11_out), .out(multiplexer_25_out), .sel(shiftcount[1]));
  Multiplexer #(.enable("false")) multiplexer_26 (
    .in0(multiplexer_10_out), .in1(multiplexer_12_out), .out(multiplexer_26_out), .sel(shiftcount[1]));
  Multiplexer #(.enable("false")) multiplexer_27 (
    .in0(multiplexer_11_out), .in1(multiplexer_13_out), .out(multiplexer_27_out), .sel(shiftcount[1]));
  Multiplexer #(.enable("false")) multiplexer_28 (
    .in0(multiplexer_12_out), .in1(multiplexer_14_out), .out(multiplexer_28_out), .sel(shiftcount[1]));
  Multiplexer #(.enable("false")) multiplexer_29 (
    .in0(multiplexer_13_out), .in1(multiplexer_15_out), .out(multiplexer_29_out), .sel(shiftcount[1]));
  Multiplexer #(.enable("false")) multiplexer_30 (
    .in0(multiplexer_14_out), .in1(multiplexer_16_out), .out(multiplexer_30_out), .sel(shiftcount[1]));
  Multiplexer #(.enable("false")) multiplexer_31 (
    .in0(multiplexer_15_out), .in1(1'b0), .out(multiplexer_31_out), .sel(shiftcount[1]));
  Multiplexer #(.enable("false")) multiplexer_32 (
    .in0(multiplexer_16_out), .in1(1'b0), .out(multiplexer_32_out), .sel(shiftcount[1]));
  Multiplexer #(.enable("false")) multiplexer_33 (
    .in0(multiplexer_17_out), .in1(multiplexer_21_out), .out(result[15]), .sel(shiftcount[2]));
  Multiplexer #(.enable("false")) multiplexer_34 (
    .in0(multiplexer_18_out), .in1(multiplexer_22_out), .out(result[14]), .sel(shiftcount[2]));
  Multiplexer #(.enable("false")) multiplexer_35 (
    .in0(multiplexer_19_out), .in1(multiplexer_23_out), .out(result[13]), .sel(shiftcount[2]));
  Multiplexer #(.enable("false")) multiplexer_36 (
    .in0(multiplexer_20_out), .in1(multiplexer_24_out), .out(result[12]), .sel(shiftcount[2]));
  Multiplexer #(.enable("false")) multiplexer_37 (
    .in0(multiplexer_21_out), .in1(multiplexer_25_out), .out(result[11]), .sel(shiftcount[2]));
  Multiplexer #(.enable("false")) multiplexer_38 (
    .in0(multiplexer_22_out), .in1(multiplexer_26_out), .out(result[10]), .sel(shiftcount[2]));
  Multiplexer #(.enable("false")) multiplexer_39 (
    .in0(multiplexer_23_out), .in1(multiplexer_27_out), .out(result[9]), .sel(shiftcount[2]));
  Multiplexer #(.enable("false")) multiplexer_40 (
    .in0(multiplexer_24_out), .in1(multiplexer_28_out), .out(result[8]), .sel(shiftcount[2]));
  Multiplexer #(.enable("false")) multiplexer_41 (
    .in0(multiplexer_25_out), .in1(multiplexer_29_out), .out(result[7]), .sel(shiftcount[2]));
  Multiplexer #(.enable("false")) multiplexer_42 (
    .in0(multiplexer_26_out), .in1(multiplexer_30_out), .out(result[6]), .sel(shiftcount[2]));
  Multiplexer #(.enable("false")) multiplexer_43 (
    .in0(multiplexer_27_out), .in1(multiplexer_31_out), .out(result[5]), .sel(shiftcount[2]));
  Multiplexer #(.enable("false")) multiplexer_44 (
    .in0(multiplexer_28_out), .in1(multiplexer_32_out), .out(result[4]), .sel(shiftcount[2]));
  Multiplexer #(.enable("false")) multiplexer_45 (
    .in0(multiplexer_29_out), .in1(1'b0), .out(result[3]), .sel(shiftcount[2]));
  Multiplexer #(.enable("false")) multiplexer_46 (
    .in0(multiplexer_30_out), .in1(1'b0), .out(result[2]), .sel(shiftcount[2]));
  Multiplexer #(.enable("false")) multiplexer_47 (
    .in0(multiplexer_31_out), .in1(1'b0), .out(result[1]), .sel(shiftcount[2]));
  Multiplexer #(.enable("false")) multiplexer_48 (
    .in0(multiplexer_32_out), .in1(1'b0), .out(result[0]), .sel(shiftcount[2]));

  // Other names for the same wires on the sheet: A0 = \input [0]; A1 = \input [1]; A2 = \input [2]; A3 = \input [3];
  //   A4 = \input [4]; A5 = \input [5]; A6 = \input [6]; A7 = \input [7]; A8 = \input [8]; A9 = \input [9];
  //   A10 = \input [10]; A11 = \input [11]; A12 = \input [12]; A13 = \input [13]; A14 = \input [14];
  //   A15 = \input [15]; S0 = result[0]; S1 = result[1]; S2 = result[2]; S3 = result[3]; S4 = result[4];
  //   S5 = result[5]; S6 = result[6]; S7 = result[7]; S8 = result[8]; S9 = result[9]; S10 = result[10];
  //   S11 = result[11]; S12 = result[12]; S13 = result[13]; S14 = result[14]; S15 = result[15];
  //   shift0 = shiftcount[0]; shift1 = shiftcount[1]; shift2 = shiftcount[2]
endmodule

module ProgramCounter (
  input  [15:0] \input ,
  input  clk,
  input  reset,
  output [15:0] \output 
);

  register register_1 (.info_in(\input ), .clock(clk), .write_enable(1'b1), .reset(reset), .info_out(\output ));
endmodule

module InstrDecode (
  input  [15:0] in1,
  output [2:0] Rd,
  output [2:0] Rs,
  output [2:0] Rt,
  output [2:0] shamt,
  output [5:0] Immed,
  output [3:0] opcode,
  output [11:0] Address
);


  assign Address = in1[11:0];
  assign Immed = in1[5:0];
  assign opcode = in1[15:12];
  assign Rd = in1[5:3];
  assign Rs = in1[11:9];
  assign Rt = in1[8:6];
  assign shamt = in1[2:0];

  // Other names for the same wires on the sheet: tun0 = in1[0]; tun1 = in1[1]; tun2 = in1[2]; tun3 = in1[3];
  //   tun4 = in1[4]; tun5 = in1[5]; tun6 = in1[6]; tun7 = in1[7]; tun8 = in1[8]; tun9 = in1[9]; tun10 = in1[10];
  //   tun11 = in1[11]; tun12 = in1[12]; tun13 = in1[13]; tun14 = in1[14]; tun15 = in1[15]
endmodule

module control (
  input  [3:0] opcode,
  output [1:0] Rdst,
  output [2:0] ALUop,
  output BRE,
  output JP,
  output DMwe,
  output Rwd,
  output ALUinB,
  output Jal,
  output Jr,
  output \output ,
  output \input ,
  output Rwe,
  output BRG
);

  wire add, addi, \and , j, \or , or_4_out, or_5_out, shl, shra, sub;
  wire [1:0] multiplexer_2_out;
  wire [2:0] multiplexer_1_out, multiplexer_3_out, multiplexer_5_out, multiplexer_6_out;

  or or_1 (Rwe, \input , Rwd, \or , \and , addi, shl, shra, sub, add, Jal);
  Decoder #(.select(4)) decoder_1 (
    .out0(\output ), .out1(\input ), .out2(Rwd), .out3(DMwe), .out4(BRE), .out5(BRG), .out6(\or ),
    .out7(\and ), .out8(addi), .out9(add), .out10(sub), .out11(shra), .out12(shl), .out13(j), .out14(Jal),
    .out15(Jr), .sel(opcode), .en(1'b1));
  or or_2 (JP, j, Jal, Jr);
  or or_3 (ALUinB, Rwd, DMwe, addi);
  Multiplexer #(.width(3), .enable("false")) multiplexer_1 (
    .in0(3'b000), .in1(3'b001), .out(multiplexer_1_out), .sel(or_4_out));
  or or_4 (or_4_out, sub, BRE, BRG, BRG);
  Multiplexer #(.width(2), .enable("false")) multiplexer_2 (
    .in0(2'b00), .in1(2'b01), .out(multiplexer_2_out), .sel(or_5_out));
  or or_5 (or_5_out, \or , \and , add, \input , sub, shra, shl);
  Multiplexer #(.width(3), .enable("false")) multiplexer_3 (
    .in0(multiplexer_1_out), .in1(3'b010), .out(multiplexer_3_out), .sel(\or ));
  Multiplexer #(.width(2), .enable("false")) multiplexer_4 (
    .in0(multiplexer_2_out), .in1(2'b10), .out(Rdst), .sel(Jal));
  Multiplexer #(.width(3), .enable("false")) multiplexer_5 (
    .in0(multiplexer_3_out), .in1(3'b011), .out(multiplexer_5_out), .sel(\and ));
  Multiplexer #(.width(3), .enable("false")) multiplexer_6 (
    .in0(multiplexer_5_out), .in1(3'b100), .out(multiplexer_6_out), .sel(shl));
  Multiplexer #(.width(3), .enable("false")) multiplexer_7 (
    .in0(multiplexer_6_out), .in1(3'b101), .out(ALUop), .sel(shra));

  // Other names for the same wires on the sheet: beq = BRE; bgt = BRG; lw = Rwd; sw = DMwe
endmodule

module rightshift (
  input  [2:0] shiftcount,
  input  [15:0] \input ,
  output [15:0] result
);

  wire multiplexer_1_out, multiplexer_2_out, multiplexer_3_out, multiplexer_4_out, multiplexer_5_out,
       multiplexer_6_out, multiplexer_7_out, multiplexer_8_out, multiplexer_9_out, multiplexer_10_out,
       multiplexer_11_out, multiplexer_12_out, multiplexer_13_out, multiplexer_14_out, multiplexer_15_out,
       multiplexer_16_out, multiplexer_17_out, multiplexer_18_out, multiplexer_19_out, multiplexer_20_out,
       multiplexer_21_out, multiplexer_22_out, multiplexer_23_out, multiplexer_24_out, multiplexer_25_out,
       multiplexer_26_out, multiplexer_27_out, multiplexer_28_out, multiplexer_29_out, multiplexer_30_out,
       multiplexer_31_out, multiplexer_32_out;

  Multiplexer #(.enable("false")) multiplexer_1 (
    .in0(\input [0]), .in1(\input [1]), .out(multiplexer_1_out), .sel(shiftcount[0]));
  Multiplexer #(.enable("false")) multiplexer_2 (
    .in0(\input [1]), .in1(\input [2]), .out(multiplexer_2_out), .sel(shiftcount[0]));
  Multiplexer #(.enable("false")) multiplexer_3 (
    .in0(\input [2]), .in1(\input [3]), .out(multiplexer_3_out), .sel(shiftcount[0]));
  Multiplexer #(.enable("false")) multiplexer_4 (
    .in0(\input [3]), .in1(\input [4]), .out(multiplexer_4_out), .sel(shiftcount[0]));
  Multiplexer #(.enable("false")) multiplexer_5 (
    .in0(\input [4]), .in1(\input [5]), .out(multiplexer_5_out), .sel(shiftcount[0]));
  Multiplexer #(.enable("false")) multiplexer_6 (
    .in0(\input [5]), .in1(\input [6]), .out(multiplexer_6_out), .sel(shiftcount[0]));
  Multiplexer #(.enable("false")) multiplexer_7 (
    .in0(\input [6]), .in1(\input [7]), .out(multiplexer_7_out), .sel(shiftcount[0]));
  Multiplexer #(.enable("false")) multiplexer_8 (
    .in0(\input [7]), .in1(\input [8]), .out(multiplexer_8_out), .sel(shiftcount[0]));
  Multiplexer #(.enable("false")) multiplexer_9 (
    .in0(\input [8]), .in1(\input [9]), .out(multiplexer_9_out), .sel(shiftcount[0]));
  Multiplexer #(.enable("false")) multiplexer_10 (
    .in0(\input [9]), .in1(\input [10]), .out(multiplexer_10_out), .sel(shiftcount[0]));
  Multiplexer #(.enable("false")) multiplexer_11 (
    .in0(\input [10]), .in1(\input [11]), .out(multiplexer_11_out), .sel(shiftcount[0]));
  Multiplexer #(.enable("false")) multiplexer_12 (
    .in0(\input [11]), .in1(\input [12]), .out(multiplexer_12_out), .sel(shiftcount[0]));
  Multiplexer #(.enable("false")) multiplexer_13 (
    .in0(\input [12]), .in1(\input [13]), .out(multiplexer_13_out), .sel(shiftcount[0]));
  Multiplexer #(.enable("false")) multiplexer_14 (
    .in0(\input [13]), .in1(\input [14]), .out(multiplexer_14_out), .sel(shiftcount[0]));
  Multiplexer #(.enable("false")) multiplexer_15 (
    .in0(\input [14]), .in1(\input [15]), .out(multiplexer_15_out), .sel(shiftcount[0]));
  Multiplexer #(.enable("false")) multiplexer_16 (
    .in0(\input [15]), .in1(\input [15]), .out(multiplexer_16_out), .sel(shiftcount[0]));
  Multiplexer #(.enable("false")) multiplexer_17 (
    .in0(multiplexer_1_out), .in1(multiplexer_3_out), .out(multiplexer_17_out), .sel(shiftcount[1]));
  Multiplexer #(.enable("false")) multiplexer_18 (
    .in0(multiplexer_2_out), .in1(multiplexer_4_out), .out(multiplexer_18_out), .sel(shiftcount[1]));
  Multiplexer #(.enable("false")) multiplexer_19 (
    .in0(multiplexer_3_out), .in1(multiplexer_5_out), .out(multiplexer_19_out), .sel(shiftcount[1]));
  Multiplexer #(.enable("false")) multiplexer_20 (
    .in0(multiplexer_4_out), .in1(multiplexer_6_out), .out(multiplexer_20_out), .sel(shiftcount[1]));
  Multiplexer #(.enable("false")) multiplexer_21 (
    .in0(multiplexer_5_out), .in1(multiplexer_7_out), .out(multiplexer_21_out), .sel(shiftcount[1]));
  Multiplexer #(.enable("false")) multiplexer_22 (
    .in0(multiplexer_6_out), .in1(multiplexer_8_out), .out(multiplexer_22_out), .sel(shiftcount[1]));
  Multiplexer #(.enable("false")) multiplexer_23 (
    .in0(multiplexer_7_out), .in1(multiplexer_9_out), .out(multiplexer_23_out), .sel(shiftcount[1]));
  Multiplexer #(.enable("false")) multiplexer_24 (
    .in0(multiplexer_8_out), .in1(multiplexer_10_out), .out(multiplexer_24_out), .sel(shiftcount[1]));
  Multiplexer #(.enable("false")) multiplexer_25 (
    .in0(multiplexer_9_out), .in1(multiplexer_11_out), .out(multiplexer_25_out), .sel(shiftcount[1]));
  Multiplexer #(.enable("false")) multiplexer_26 (
    .in0(multiplexer_10_out), .in1(multiplexer_12_out), .out(multiplexer_26_out), .sel(shiftcount[1]));
  Multiplexer #(.enable("false")) multiplexer_27 (
    .in0(multiplexer_11_out), .in1(multiplexer_13_out), .out(multiplexer_27_out), .sel(shiftcount[1]));
  Multiplexer #(.enable("false")) multiplexer_28 (
    .in0(multiplexer_12_out), .in1(multiplexer_14_out), .out(multiplexer_28_out), .sel(shiftcount[1]));
  Multiplexer #(.enable("false")) multiplexer_29 (
    .in0(multiplexer_13_out), .in1(multiplexer_15_out), .out(multiplexer_29_out), .sel(shiftcount[1]));
  Multiplexer #(.enable("false")) multiplexer_30 (
    .in0(multiplexer_14_out), .in1(multiplexer_16_out), .out(multiplexer_30_out), .sel(shiftcount[1]));
  Multiplexer #(.enable("false")) multiplexer_31 (
    .in0(multiplexer_15_out), .in1(\input [15]), .out(multiplexer_31_out), .sel(shiftcount[1]));
  Multiplexer #(.enable("false")) multiplexer_32 (
    .in0(multiplexer_16_out), .in1(\input [15]), .out(multiplexer_32_out), .sel(shiftcount[1]));
  Multiplexer #(.enable("false")) multiplexer_33 (
    .in0(multiplexer_17_out), .in1(multiplexer_21_out), .out(result[0]), .sel(shiftcount[2]));
  Multiplexer #(.enable("false")) multiplexer_34 (
    .in0(multiplexer_18_out), .in1(multiplexer_22_out), .out(result[1]), .sel(shiftcount[2]));
  Multiplexer #(.enable("false")) multiplexer_35 (
    .in0(multiplexer_19_out), .in1(multiplexer_23_out), .out(result[2]), .sel(shiftcount[2]));
  Multiplexer #(.enable("false")) multiplexer_36 (
    .in0(multiplexer_20_out), .in1(multiplexer_24_out), .out(result[3]), .sel(shiftcount[2]));
  Multiplexer #(.enable("false")) multiplexer_37 (
    .in0(multiplexer_21_out), .in1(multiplexer_25_out), .out(result[4]), .sel(shiftcount[2]));
  Multiplexer #(.enable("false")) multiplexer_38 (
    .in0(multiplexer_22_out), .in1(multiplexer_26_out), .out(result[5]), .sel(shiftcount[2]));
  Multiplexer #(.enable("false")) multiplexer_39 (
    .in0(multiplexer_23_out), .in1(multiplexer_27_out), .out(result[6]), .sel(shiftcount[2]));
  Multiplexer #(.enable("false")) multiplexer_40 (
    .in0(multiplexer_24_out), .in1(multiplexer_28_out), .out(result[7]), .sel(shiftcount[2]));
  Multiplexer #(.enable("false")) multiplexer_41 (
    .in0(multiplexer_25_out), .in1(multiplexer_29_out), .out(result[8]), .sel(shiftcount[2]));
  Multiplexer #(.enable("false")) multiplexer_42 (
    .in0(multiplexer_26_out), .in1(multiplexer_30_out), .out(result[9]), .sel(shiftcount[2]));
  Multiplexer #(.enable("false")) multiplexer_43 (
    .in0(multiplexer_27_out), .in1(multiplexer_31_out), .out(result[10]), .sel(shiftcount[2]));
  Multiplexer #(.enable("false")) multiplexer_44 (
    .in0(multiplexer_28_out), .in1(multiplexer_32_out), .out(result[11]), .sel(shiftcount[2]));
  Multiplexer #(.enable("false")) multiplexer_45 (
    .in0(multiplexer_29_out), .in1(\input [15]), .out(result[12]), .sel(shiftcount[2]));
  Multiplexer #(.enable("false")) multiplexer_46 (
    .in0(multiplexer_30_out), .in1(\input [15]), .out(result[13]), .sel(shiftcount[2]));
  Multiplexer #(.enable("false")) multiplexer_47 (
    .in0(multiplexer_31_out), .in1(\input [15]), .out(result[14]), .sel(shiftcount[2]));
  Multiplexer #(.enable("false")) multiplexer_48 (
    .in0(multiplexer_32_out), .in1(\input [15]), .out(result[15]), .sel(shiftcount[2]));

  // Other names for the same wires on the sheet: A0 = \input [0]; A1 = \input [1]; A2 = \input [2]; A3 = \input [3];
  //   A4 = \input [4]; A5 = \input [5]; A6 = \input [6]; A7 = \input [7]; A8 = \input [8]; A9 = \input [9];
  //   A10 = \input [10]; A11 = \input [11]; A12 = \input [12]; A13 = \input [13]; A14 = \input [14];
  //   A15 = \input [15]; S0 = result[0]; S1 = result[1]; S2 = result[2]; S3 = result[3]; S4 = result[4];
  //   S5 = result[5]; S6 = result[6]; S7 = result[7]; S8 = result[8]; S9 = result[9]; S10 = result[10];
  //   S11 = result[11]; S12 = result[12]; S13 = result[13]; S14 = result[14]; S15 = result[15];
  //   shift0 = shiftcount[0]; shift1 = shiftcount[1]; shift2 = shiftcount[2]
endmodule

module memory_latch (
  input  [15:0] address,
  input  WE,
  input  clk,
  input  [15:0] data_in,
  output [15:0] address_latched,
  output WE_latched,
  output OE_latched,
  output [15:0] data_in_latched
);

  wire d_ff_1_q;
  wire [15:0] register_1_q;

  Register #(.width(16), .trigger("falling")) register_1 (
    .D(address), .en(WE), .clk(clk), .Q(register_1_q));  // open: clr
  Register #(.width(16), .trigger("falling")) register_2 (
    .D(data_in), .en(WE), .clk(clk), .Q(data_in_latched));  // open: clr
  D_Flip_Flop #(.trigger("falling")) d_ff_1 (.D(WE), .clk(clk), .Q(d_ff_1_q));  // open: Qn, preset, reset
  Multiplexer #(.width(16), .enable("false")) multiplexer_1 (
    .in0(address), .in1(register_1_q), .out(address_latched), .sel(d_ff_1_q));
  and and_1 (WE_latched, clk, d_ff_1_q);
  not not_1 (OE_latched, WE_latched);
endmodule
